# Fritzing sketch Schematic Diagram - Source File (saved by Fritzing 0.9.4)

parts:
  S1 = H-Bridge with L298N
  M1 = DC Motor
  M2 = DC Motor
  M3 = DC Motor
  M4 = DC Motor
  S2 = H-Bridge with L298N
  Part1 = Arduino Mega 2560 (Rev3)
  M5 = DC Motor
  M6 = DC Motor
  J1 = Basic Servo
  PWM1 = PCA9685 16x12-bit PWM Breakout
  J2 = Basic Servo
  J3 = Basic Servo

nets:
  N1: S1.ENA, Part1.D3_PWM
  N2: S1.IN1, Part1.D49
  N3: S1.IN2, Part1.D51
  N4: S1.IN3, Part1.D53
  GND: S1.IN4, Part1.GND, J1.gnd, PWM1.no_name_yet#501, PWM1.no_name_yet#701, PWM1.no_name_yet#1000, PWM1.no_name_yet#1007, PWM1.no_name_yet#1015, J2.gnd, J3.gnd
  N5: S1.ENB, Part1.D2_PWM
  N6: S1.M1-01, M2.pin_2
  N7: S1.M1-02, M1.pin_1
  N8: S1.M2-01, M3.pin_1
  N9: S1.M2-02, M4.pin_2
  N10: S2.ENA, Part1.D5_PWM
  N11: S2.IN1, Part1.D41
  N12: S2.IN2, Part1.D43
  N13: S2.IN3, Part1.D45
  N14: S2.IN4, Part1.D47
  N15: S2.ENB, Part1.D4_PWM
  N16: S2.M1-01, M6.pin_2
  N17: S2.M1-02, M6.pin_1
  N18: S2.M2-01, M5.pin_2
  N19: S2.M2-02, M5.pin_1
  N20: Part1.D21/SCL, PWM1.no_name_yet#503
  N21: Part1.D20/SDA, PWM1.no_name_yet#504
  N22: Part1.5V, PWM1.no_name_yet#505
  VCC: J1.vcc, PWM1.no_name_yet#100, PWM1.no_name_yet#107, PWM1.no_name_yet#115, PWM1.no_name_yet#706, J2.vcc, J3.vcc
  N23: J1.pulse, PWM1.no_name_yet#0
  N24: PWM1.no_name_yet#7, J2.pulse
  N25: PWM1.no_name_yet#15, J3.pulse

notes:
  12 V Power Supply
  5 V Power Supply

custom parts:
  H-Bridge with L298N: h-bridge
